# Fritzing sketch FeatherHumTempDew (saved by Fritzing 0.9.3b)
breadboards: 1

parts:
  Part1 = TMP007 Thermopile Sensor
  Part2 = Adafruit Feather HUZZAH ESP8266 [part_number="Adafruit #2821"]
  DHT1 = DHT22 Humidity and Temperature Sensor
  R1 = Resistor [tolerance=±5% resistance=220 package=THT]

nets:
  VCC: Part1.VCC, Part2.3.3V, DHT1.VDD, R1.Pin_1
  GND: Part1.GND, Part2.GND, DHT1.GND
  N1: Part1.SDA, Part2.GPIO4/SDA
  N2: Part1.SCL, Part2.GPIO5/SCL
  N3: Part2.GPIO12/MISO, DHT1.DATA, R1.Pin_0

custom parts:
  TMP007 Thermopile Sensor: Unlike most of the other temperature sensors we have, this breakout has a really cool IR sensor from TI that can measure the temperature of an object without touching it! The TMP007 is the latest thermopile sensor from TI, and is an update of the TMP006. The internal math engine does all the temperature calculations so its easier to integrate - you can read the die and target temperatures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
  Adafruit Feather HUZZAH ESP8266: his is the Adafruit Feather HUZZAH ESP8266 - our take on an 'all-in-one' ESP8266 WiFi development board with built in USB and battery charging. Its an ESP8266 WiFi module with all the extras you need, ready to rock! We have other boards in the Feather family, check'em out here. At the Feather HUZZAH's heart is an ESP8266 WiFi microcontroller clocked at 80 MHz and at 3.3V logic. This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
